// Logisim project or.circ as structural Verilog: 1 circuit, main circuit main
module main (
  input  A,
  input  B,
  output A_B
);

  wire nand_1_out, nand_2_out;

  nand nand_1 (nand_1_out, A, A);
  nand nand_2 (nand_2_out, B, B);
  nand nand_3 (A_B, nand_1_out, nand_2_out);

  // Notes on the sheet:
  //   A: pull=up
endmodule
