// Logisim project somma.circ as structural Verilog: 1 circuit, main circuit main
module main (
  input  A,
  input  B,
  output A_XOR_B,
  output A_AND_B
);

  wire nand_1_out, nand_2_out, nand_3_out;

  nand nand_1 (nand_1_out, A, B);
  nand nand_2 (nand_2_out, A, nand_1_out);
  nand nand_3 (nand_3_out, nand_1_out, B);
  nand nand_4 (A_XOR_B, nand_2_out, nand_3_out);
  nand nand_5 (A_AND_B, nand_1_out, nand_1_out);

  // Notes on the sheet:
  //   bit più significativo
  //   bit meno significativo
endmodule
