// Logisim project D-Latch.circ as structural Verilog: 1 circuit, main circuit main
module main (
  input  D,
  input  in_2,
  output Q,
  output QBAR
);

  wire nand_1_out, nand_2_out, nand_3_out;

  nand nand_1 (nand_1_out, D, D);
  nand nand_2 (nand_2_out, D, in_2);
  nand nand_3 (nand_3_out, in_2, nand_1_out);
  nand nand_4 (Q, nand_2_out, QBAR);
  nand nand_5 (QBAR, Q, nand_3_out);
endmodule
