// Logisim project no-fnge-cazzo.circ as structural Verilog: 1 circuit, main circuit main
module main (
  input  in_1,
  output out_2,
  output out_3,
  output out_4,
  output out_5
);

  wire clock_1_out, nand_1_out, nand_2_out, nand_3_out, pull_resistor_1_node;

  nand nand_1 (nand_1_out, nand_3_out, nand_3_out);
  nand nand_2 (nand_2_out, nand_1_out, in_1);
  nand nand_3 (nand_3_out, out_5, out_4);
  J_K_Flip_Flop j_k_ff_1 (.clk(1'b1), .Q(out_3), .en(clock_1_out), .reset(clock_1_out));  // open: J, K, Qn, preset
  Clock clock_1 (.out(clock_1_out));
  Pull_Resistor pull_resistor_1 (.node(pull_resistor_1_node));
  J_K_Flip_Flop j_k_ff_2 (.clk(1'b1), .Q(out_4), .en(out_3));  // open: J, K, Qn, preset, reset
  Pull_Resistor pull_resistor_2 (.node(pull_resistor_1_node));
  J_K_Flip_Flop j_k_ff_3 (.clk(1'b1), .Q(out_2), .en(out_4));  // open: J, K, Qn, preset, reset
  Pull_Resistor pull_resistor_3 (.node(pull_resistor_1_node));
  J_K_Flip_Flop j_k_ff_4 (.clk(1'b1), .Q(out_5), .en(out_2));  // open: J, K, Qn, preset, reset
  Pull_Resistor pull_resistor_4 (.node(pull_resistor_1_node));
  // also tied to GND on the sheet: pull_resistor_1_node
endmodule
