// Logisim project f.circ as structural Verilog: 2 circuits, main circuit main
module main (
  input  in_1
);

  wire and_1_out, clock_1_out, clock_2_out, d_ff_1_q, d_ff_1_qn, d_ff_2_q, d_ff_2_qn, d_ff_3_q, d_ff_3_qn,
       d_ff_4_q, d_ff_4_qn, nand_1_out, nand_2_out;

  nand nand_1 (nand_1_out, d_ff_2_q, d_ff_1_q);
  nand nand_2 (nand_2_out, d_ff_4_q, d_ff_3_q);
  Clock clock_1 (.out(clock_1_out));
  Clock clock_2 (.out(clock_2_out));
  D_Flip_Flop d_ff_1 (.clk(clock_1_out), .D(nand_1_out), .Q(d_ff_1_q), .Qn(d_ff_1_qn));  // open: preset, en, reset
  D_Flip_Flop d_ff_2 (.clk(clock_1_out), .D(d_ff_1_q), .Q(d_ff_2_q), .Qn(d_ff_2_qn));  // open: preset, en, reset
  D_Flip_Flop d_ff_3 (.clk(clock_2_out), .D(nand_2_out), .Q(d_ff_3_q), .Qn(d_ff_3_qn));  // open: preset, en, reset
  D_Flip_Flop d_ff_4 (.clk(clock_2_out), .D(d_ff_3_q), .Q(d_ff_4_q), .Qn(d_ff_4_qn));  // open: preset, en, reset
  LED led_1 (.in(d_ff_3_qn));
  LED led_2 (.in(d_ff_4_q));
  LED led_3 (.in(d_ff_4_qn));
  and and_1 (and_1_out, d_ff_2_q, in_1);
  LED led_4 (.in(d_ff_1_qn));
  LED led_5 (.in(and_1_out));
  LED led_6 (.in(d_ff_2_qn));

  // Notes on the sheet:
  //   B0
  //   B1
endmodule

module a (
  input  b1,
  input  b0,
  input  En,
  output B1_2,
  output B0_2
);

  wire and_2_out, and_3_out, not_1_out, not_2_out, not_3_out, not_4_out;

  and and_1 (B1_2, b0, En);
  not not_1 (not_1_out, b1);
  not not_2 (not_2_out, b0);
  not not_3 (not_3_out, b0);
  not not_4 (not_4_out, En);
  and and_2 (and_2_out, not_1_out, not_2_out);
  and and_3 (and_3_out, not_3_out, not_4_out);
  or or_1 (B0_2, and_2_out, and_3_out);
endmodule
