// Logisim project semaforaabb.circ as structural Verilog: 1 circuit, main circuit main
module main (
);

  wire and_1_out, and_2_out, and_3_out, clock_1_out, clock_2_out, clock_3_out, clock_4_out, d_ff_1_q,
       d_ff_1_qn, d_ff_2_q, d_ff_2_qn, d_ff_3_q, d_ff_3_qn, d_ff_4_q, d_ff_4_qn, d_ff_5_q, d_ff_5_qn,
       d_ff_6_q, d_ff_6_qn, d_ff_7_q, d_ff_7_qn, d_ff_8_q, d_ff_8_qn, nand_1_out, nand_2_out, nand_3_out,
       nand_4_out, nand_5_out;

  nand nand_1 (nand_1_out, d_ff_5_qn, d_ff_6_qn);
  and and_1 (and_1_out, d_ff_3_qn, d_ff_4_qn);
  and and_2 (and_2_out, d_ff_3_q, d_ff_4_qn);
  nand nand_2 (nand_2_out, nand_1_out, nand_1_out);
  nand nand_3 (nand_3_out, d_ff_5_q, d_ff_6_qn);
  Clock clock_1 (.out(clock_1_out));
  and and_3 (and_3_out, d_ff_1_qn, d_ff_2_qn);
  Clock clock_2 (.out(clock_2_out));
  Clock clock_3 (.out(clock_3_out));
  nand nand_4 (nand_4_out, nand_3_out, nand_3_out);
  D_Flip_Flop d_ff_1 (.clk(clock_2_out), .D(d_ff_2_q), .Q(d_ff_1_q), .Qn(d_ff_1_qn));  // open: preset, en, reset
  D_Flip_Flop d_ff_2 (.clk(clock_2_out), .D(and_3_out), .Q(d_ff_2_q), .Qn(d_ff_2_qn));  // open: preset, en, reset
  D_Flip_Flop d_ff_3 (.clk(clock_3_out), .D(and_1_out), .Q(d_ff_3_q), .Qn(d_ff_3_qn));  // open: preset, en, reset
  D_Flip_Flop d_ff_4 (.clk(clock_3_out), .D(and_2_out), .Q(d_ff_4_q), .Qn(d_ff_4_qn));  // open: preset, en, reset
  D_Flip_Flop d_ff_5 (.clk(clock_1_out), .D(nand_2_out), .Q(d_ff_5_q), .Qn(d_ff_5_qn));  // open: preset, en, reset
  D_Flip_Flop d_ff_6 (.clk(clock_1_out), .D(nand_4_out), .Q(d_ff_6_q), .Qn(d_ff_6_qn));  // open: preset, en, reset
  LED led_1 (.in(d_ff_4_q));
  LED led_2 (.in(d_ff_3_q));
  LED led_3 (.in(d_ff_4_qn));
  LED led_4 (.in(d_ff_6_q));
  LED led_5 (.in(d_ff_5_q));
  LED led_6 (.in(d_ff_6_qn));
  LED led_7 (.in(d_ff_1_q));
  LED led_8 (.in(d_ff_2_q));
  LED led_9 (.in(d_ff_1_qn));
  Clock clock_4 (.out(clock_4_out));
  nand nand_5 (nand_5_out, d_ff_7_q, d_ff_8_q);
  D_Flip_Flop d_ff_7 (.clk(clock_4_out), .D(nand_5_out), .Q(d_ff_7_q), .Qn(d_ff_7_qn));  // open: preset, en, reset
  D_Flip_Flop d_ff_8 (.clk(clock_4_out), .D(d_ff_7_q), .Q(d_ff_8_q), .Qn(d_ff_8_qn));  // open: preset, en, reset
  LED led_10 (.in(d_ff_7_qn));
  LED led_11 (.in(d_ff_8_q));
  LED led_12 (.in(d_ff_8_qn));

  // Notes on the sheet:
  //   B1
  //   B0
  //   LED ROSSO
  //   LED GIALLO
  //   LED VERDE
endmodule
