// Logisim project semaforo-sinc.circ as structural Verilog: 1 circuit, main circuit main
module main (
  input  in_1,
  input  in_2,
  input  in_3,
  input  in_4
);

  wire and_1_out, and_2_out, and_3_out, and_4_out, and_5_out, and_6_out, and_7_out, and_8_out, and_9_out,
       and_10_out, clock_1_out, clock_2_out, clock_3_out, clock_4_out, d_ff_1_qn, d_ff_2_qn, d_ff_3_q,
       d_ff_3_qn, d_ff_4_q, d_ff_4_qn, d_ff_5_q, d_ff_5_qn, d_ff_6_q, d_ff_6_qn, d_ff_7_q, d_ff_7_qn,
       d_ff_8_q, d_ff_8_qn, d_ff_9_qn, d_ff_10_q, d_ff_10_qn, d_ff_11_q, d_ff_11_qn, d_ff_12_qn, nand_1_out,
       nand_2_out, nand_3_out, nand_4_out, nand_5_out, nand_6_out, nand_7_out, nand_8_out;

  Clock clock_1 (.out(clock_1_out));
  Clock clock_2 (.out(clock_2_out));
  nand nand_1 (nand_1_out, d_ff_5_qn, d_ff_6_qn);
  nand nand_2 (nand_2_out, d_ff_5_q, d_ff_6_qn);
  D_Flip_Flop d_ff_1 (.clk(clock_1_out), .D(in_1), .Qn(d_ff_1_qn));  // open: Q, preset, en, reset
  D_Flip_Flop d_ff_2 (.clk(clock_2_out), .D(in_3), .Qn(d_ff_2_qn));  // open: Q, preset, en, reset
  nand nand_3 (nand_3_out, nand_1_out, nand_1_out);
  nand nand_4 (nand_4_out, nand_2_out, nand_2_out);
  and and_1 (and_1_out, d_ff_3_qn, d_ff_4_qn);
  and and_2 (and_2_out, d_ff_3_q, d_ff_4_qn);
  nand nand_5 (nand_5_out, nand_4_out, d_ff_1_qn);
  and and_3 (and_3_out, and_2_out, d_ff_2_qn);
  nand nand_6 (nand_6_out, nand_5_out, nand_5_out);
  D_Flip_Flop d_ff_3 (.clk(clock_2_out), .D(and_1_out), .Q(d_ff_3_q), .Qn(d_ff_3_qn));  // open: preset, en, reset
  D_Flip_Flop d_ff_4 (.clk(clock_2_out), .D(and_3_out), .Q(d_ff_4_q), .Qn(d_ff_4_qn));  // open: preset, en, reset
  D_Flip_Flop d_ff_5 (.clk(clock_1_out), .D(nand_3_out), .Q(d_ff_5_q), .Qn(d_ff_5_qn));  // open: preset, en, reset
  D_Flip_Flop d_ff_6 (.clk(clock_1_out), .D(nand_6_out), .Q(d_ff_6_q), .Qn(d_ff_6_qn));  // open: preset, en, reset
  nand nand_7 (nand_7_out, d_ff_6_qn, d_ff_1_qn);
  and and_4 (and_4_out, d_ff_4_qn, d_ff_2_qn);
  nand nand_8 (nand_8_out, nand_7_out, nand_7_out);
  LED led_1 (.in(d_ff_4_q));
  LED led_2 (.in(d_ff_3_q));
  LED led_3 (.in(and_4_out));
  LED led_4 (.in(d_ff_6_q));
  LED led_5 (.in(d_ff_5_q));
  LED led_6 (.in(nand_8_out));
  and and_5 (and_5_out, d_ff_8_q, d_ff_9_qn);
  and and_6 (and_6_out, d_ff_7_qn, d_ff_8_qn);
  Clock clock_3 (.out(clock_3_out));
  and and_7 (and_7_out, d_ff_10_qn, d_ff_11_qn);
  Clock clock_4 (.out(clock_4_out));
  D_Flip_Flop d_ff_7 (.clk(clock_3_out), .D(and_5_out), .Q(d_ff_7_q), .Qn(d_ff_7_qn));  // open: preset, en, reset
  D_Flip_Flop d_ff_8 (.clk(clock_3_out), .D(and_6_out), .Q(d_ff_8_q), .Qn(d_ff_8_qn));  // open: preset, en, reset
  D_Flip_Flop d_ff_9 (.clk(clock_3_out), .D(in_2), .Qn(d_ff_9_qn));  // open: Q, preset, en, reset
  D_Flip_Flop d_ff_10 (.clk(clock_4_out), .D(d_ff_11_q), .Q(d_ff_10_q), .Qn(d_ff_10_qn));  // open: preset, en, reset
  D_Flip_Flop d_ff_11 (.clk(clock_4_out), .D(and_7_out), .Q(d_ff_11_q), .Qn(d_ff_11_qn));  // open: preset, en, reset
  D_Flip_Flop d_ff_12 (.clk(clock_4_out), .D(in_4), .Qn(d_ff_12_qn));  // open: Q, preset, en, reset
  LED led_7 (.in(d_ff_7_q));
  LED led_8 (.in(d_ff_8_q));
  and and_8 (and_8_out, d_ff_7_qn, d_ff_9_qn);
  LED led_9 (.in(and_8_out));
  LED led_10 (.in(and_9_out));
  and and_9 (and_9_out, d_ff_10_q, d_ff_12_qn);
  LED led_11 (.in(d_ff_11_q));
  LED led_12 (.in(and_10_out));
  and and_10 (and_10_out, d_ff_10_qn, d_ff_12_qn);

  // Notes on the sheet:
  //   B1
  //   B0
  //   B1
  //   B0
  //   funziona
  //   non solito periodo
endmodule
